# Fritzing sketch EcoControl (saved by Fritzing 0.9.3b)
breadboards: 1

parts:
  L298N_motor_control_FAN1_2 = L298N_MC
  L298N_motor_control_FAN3_4 = L298N_MC
  L298N_motor_control_Window = L298N_MC
  Raspberry_Pi_1 = Raspberry Pi 3 [part_number=RPI-3-V1.2]
  S_Window_switch = Momentary Switch [package=ksa_sealed_tac_switch]
  M5_Window_Actuator = DC Motor
  M1_Fan1 = DC Motor
  M2_Fan2 = DC Motor
  M3_Fan3 = DC Motor
  M4_Fan4 = DC Motor
  U1_MF_relay = RELAY [package=relay-g5q]
  DS1 = DS18B20 1-Wire Temperature Sensor [part_number=DS18B20]
  R1 = Resistor [tolerance=±5% resistance=4.7k package="1206 [SMD]"]
  M6_MainFan = DC Motor
  Opamp1_3_3v_to_5v = IC, SIP package, 18 pins [chip_label=Opamp]
  U_12v_Battery = BATTERY-2 [package=battery-aaa]
  U_5v_supply = BATTERY-2 [package=battery-aaa]
  U2_unused_relay = RELAY [package=relay-g5q]

nets:
  N1: L298N_motor_control_FAN1_2.IN2#0, L298N_motor_control_FAN3_4.IN2#0, Opamp1_3_3v_to_5v.pin2
  GND: L298N_motor_control_FAN1_2.IN2#1, L298N_motor_control_FAN1_2.GND, L298N_motor_control_FAN3_4.IN2#1, L298N_motor_control_FAN3_4.GND, L298N_motor_control_Window.GND, Raspberry_Pi_1.GND, U1_MF_relay.COIL2, DS1.GND, M6_MainFan.pin_2, Opamp1_3_3v_to_5v.pin9, U_12v_Battery.+1, U_5v_supply.+2, U2_unused_relay.COIL2
  N2: L298N_motor_control_FAN1_2.ENA, L298N_motor_control_FAN1_2.5V+, L298N_motor_control_FAN3_4.ENA, L298N_motor_control_FAN3_4.5V+, L298N_motor_control_Window.5V+, U_5v_supply.-2
  VIN: L298N_motor_control_FAN1_2.Vin, L298N_motor_control_FAN3_4.Vin, L298N_motor_control_Window.Vin, U1_MF_relay.NO, Opamp1_3_3v_to_5v.pin10, U_12v_Battery.-1
  N3: L298N_motor_control_FAN1_2.B1out, M1_Fan1.pin_2, M2_Fan2.pin_2
  N4: L298N_motor_control_FAN1_2.A1out, M1_Fan1.pin_1, M2_Fan2.pin_1
  N5: L298N_motor_control_FAN3_4.B1out, M3_Fan3.pin_2, M4_Fan4.pin_2
  N6: L298N_motor_control_FAN3_4.A1out, M3_Fan3.pin_1, M4_Fan4.pin_1
  N7: L298N_motor_control_Window.IN2#0, Opamp1_3_3v_to_5v.pin4
  N8: L298N_motor_control_Window.IN2#1, Opamp1_3_3v_to_5v.pin6
  N9: L298N_motor_control_Window.ENA, Opamp1_3_3v_to_5v.pin8
  N10: L298N_motor_control_Window.B1out, M5_Window_Actuator.pin_2
  N11: L298N_motor_control_Window.A1out, M5_Window_Actuator.pin_1
  N12: Raspberry_Pi_1.GPIO4, DS1.DQ
  3V3: Raspberry_Pi_1.3V3, DS1.VDD, R1.Pin_0
  N13: Raspberry_Pi_1.ID_SD, Opamp1_3_3v_to_5v.pin15
  N14: Raspberry_Pi_1.GPIO5, Opamp1_3_3v_to_5v.pin17
  N15: Raspberry_Pi_1.GPIO6, Opamp1_3_3v_to_5v.pin7
  N16: Raspberry_Pi_1.GPIO13, Opamp1_3_3v_to_5v.pin5
  N17: Raspberry_Pi_1.GPIO19, Opamp1_3_3v_to_5v.pin3
  N18: Raspberry_Pi_1.GPIO26, Opamp1_3_3v_to_5v.pin1
  N19: Raspberry_Pi_1.GPIO21, S_Window_switch.3
  N20: S_Window_switch.1, R1.Pin_1
  N21: U1_MF_relay.MAIN, M6_MainFan.pin_1
  N22: U1_MF_relay.COIL1, Opamp1_3_3v_to_5v.pin16
  N23: Opamp1_3_3v_to_5v.pin18, U2_unused_relay.COIL1

notes:
  * The DS18B20 sensor actually consists of multiple sensors put in parallel, as they use one wire.
  * The motor controllers are actually a L298N mounted on a PCB with some addtional hardware. The Edgy was used because its pinout is similar.
  EcoDome Controller, Schematic of how the controller is connected to the sensors and actuators., 1.1

custom parts:
  L298N_MC: Motor controller with a L298N as its core.
